# Fritzing sketch matias_FK303_Raspberry_Pico (saved by Fritzing 0.9.9b)
circuit board: 10.3cm x 2.1cm
breadboards: 1

parts:
  IC1 = Raspberry Pi Pico  # not connected
  J8 = female pin header, 20 pins [form="♀ (female)"]
  J9 = female pin header, 20 pins [form="♀ (female)"]
  J4 = male pin header, 17 pins [form="♂ (male)"]
  J7 = male pin header, 17 pins [form="♂ (male)"]

nets:
  N1: J8.pin1, J7.pin11
  N2: J8.pin2, J7.pin12
  N3: J8.pin4, J7.pin13
  N4: J8.pin5, J7.pin14
  N5: J8.pin6, J4.pin16
  N6: J8.pin7, J4.pin15
  N7: J8.pin9, J4.pin14
  N8: J8.pin10, J4.pin13
  N9: J8.pin11, J4.pin12
  N10: J8.pin12, J4.pin11
  N11: J8.pin14, J4.pin10
  N12: J8.pin15, J4.pin9
  N13: J8.pin16, J4.pin8
  N14: J8.pin17, J4.pin7
  N15: J8.pin19, J4.pin6
  N16: J8.pin20, J4.pin5
  N17: J9.pin5, J9.pin9, J7.pin9, J7.pin17
  N18: J9.pin7, J7.pin10
  N19: J9.pin10, J7.pin8
  N20: J9.pin12, J7.pin7
  N21: J9.pin14, J7.pin6
  N22: J9.pin15, J7.pin5
  N23: J9.pin16, J7.pin4
  N24: J9.pin17, J7.pin3
  N25: J9.pin18, J4.pin17, J7.pin16
  N26: J9.pin19, J7.pin2
  N27: J9.pin20, J7.pin1

notes:
  Maggie & Thomas © 2021, v02
  Matias Quiet Pro Mini USB PCB replacement

custom parts:
  Raspberry Pi Pico: Raspberry Pi Pico. Based around the RP2040 microcontroller the Pico is a low cost microcontroller device bringing Raspberry Pi quality, cost, and easy of use to the microcontroller space. Jan 2021, Split part in to two versions: tht (this one) and SMD. This one will drill holes for a .1 in header in pcb to allow plugging in the module as well as providing pads to solder the module to the top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
